// Logisim project ALU-Hack-test.circ as structural Verilog: 1 circuit, main circuit main
module main (
  input  ZX,
  input  NX,
  input  ZY,
  input  NY,
  input  F,
  input  NO,
  input  [7:0] in_7,
  input  [7:0] in_8,
  output [7:0] out_9,
  output NG,
  output ZR
);

  wire [7:0] adder_1_out, and_1_out, multiplexer_1_out, multiplexer_2_out, multiplexer_3_out,
       multiplexer_4_out, multiplexer_5_out, not_1_out, not_2_out, not_3_out;

  Multiplexer #(.width(8), .enable("false")) multiplexer_1 (
    .in0(in_7), .in1({8{1'b0}}), .out(multiplexer_1_out), .sel(ZX));
  Multiplexer #(.width(8), .enable("false")) multiplexer_2 (
    .in0(in_8), .in1({8{1'b0}}), .out(multiplexer_2_out), .sel(ZY));
  assign not_1_out = ~multiplexer_1_out;  // NOT_Gate not_1, 8 bits wide
  assign not_2_out = ~multiplexer_2_out;  // NOT_Gate not_2, 8 bits wide
  Multiplexer #(.width(8), .enable("false")) multiplexer_3 (
    .in0(multiplexer_1_out), .in1(not_1_out), .out(multiplexer_3_out), .sel(NX));
  Multiplexer #(.width(8), .enable("false")) multiplexer_4 (
    .in0(multiplexer_2_out), .in1(not_2_out), .out(multiplexer_4_out), .sel(NY));
  assign and_1_out = multiplexer_3_out & multiplexer_4_out;  // AND_Gate and_1, 8 bits wide
  Adder adder_1 (.a(multiplexer_3_out), .b(multiplexer_4_out), .out(adder_1_out));  // open: cin, cout
  nor nor_1 (ZR, NG, out_9[6], out_9[5], out_9[4], out_9[3], out_9[2], out_9[1], out_9[0]);
  Multiplexer #(.width(8), .enable("false")) multiplexer_5 (
    .in0(and_1_out), .in1(adder_1_out), .out(multiplexer_5_out), .sel(F));
  assign not_3_out = ~multiplexer_5_out;  // NOT_Gate not_3, 8 bits wide
  Multiplexer #(.width(8), .enable("false")) multiplexer_6 (
    .in0(multiplexer_5_out), .in1(not_3_out), .out({NG, out_9[6:0]}), .sel(NO));

  assign out_9[7] = NG;
endmodule
