// Logisim project LittleDrop.circ as structural Verilog: 27 circuits, main circuit main
module main (
  input  [7:0] in_1,
  input  in_2,
  input  [4:0] in_3,
  output [7:0] out_4
);

  wire clock_1_out;

  Clock clock_1 (.out(clock_1_out));
  RAM32 ram32_1 (.In(in_1), .Load(in_2), .Clock(clock_1_out), .Sel(in_3), .Out(out_4));
endmodule

module RAM32 (
  input  [7:0] In,
  input  Load,
  input  Clock,
  input  [4:0] Sel,
  output [7:0] Out
);

  wire dmux4way_1_a, dmux4way_1_b, dmux4way_1_c, dmux4way_1_d;
  wire [7:0] ram8_1_out, ram8_2_out, ram8_3_out, ram8_4_out;

  Dmux4Way dmux4way_1 (
    .In(Load), .Sel(Sel[4:3]), .A(dmux4way_1_a), .B(dmux4way_1_b), .C(dmux4way_1_c), .D(dmux4way_1_d));
  RAM8 ram8_1 (.Clock(Clock), .In(In), .Load(dmux4way_1_a), .Sel(Sel[2:0]), .Out(ram8_1_out));
  RAM8 ram8_2 (.Clock(Clock), .In(In), .Load(dmux4way_1_b), .Sel(Sel[2:0]), .Out(ram8_2_out));
  RAM8 ram8_3 (.Clock(Clock), .In(In), .Load(dmux4way_1_c), .Sel(Sel[2:0]), .Out(ram8_3_out));
  RAM8 ram8_4 (.Clock(Clock), .In(In), .Load(dmux4way_1_d), .Sel(Sel[2:0]), .Out(ram8_4_out));
  // Probe on Sel[2:0]
  // Probe on ram8_1_out
  // Probe on ram8_2_out
  // Probe on ram8_3_out
  // Probe on ram8_4_out
  // Probe on Sel[4:3]
  Mux4Way8 mux4way8_1 (
    .In0(ram8_1_out), .In1(ram8_2_out), .In2(ram8_3_out), .In3(ram8_4_out), .in_5(Sel[4:3]), .Out(Out));
endmodule

module RAM8 (
  input  Clock,
  input  [7:0] In,
  input  Load,
  input  [2:0] Sel,
  output [7:0] Out
);

  wire dmux8way_1_a, dmux8way_1_b, dmux8way_1_c, dmux8way_1_d, dmux8way_1_e, dmux8way_1_f, dmux8way_1_g,
       dmux8way_1_h;
  wire [7:0] n8_bit_register_1_out, n8_bit_register_2_out, n8_bit_register_3_out, n8_bit_register_4_out,
       n8_bit_register_5_out, n8_bit_register_6_out, n8_bit_register_7_out, n8_bit_register_8_out;

  Dmux8Way dmux8way_1 (
    .In(Load), .in_2(Sel), .A(dmux8way_1_a), .B(dmux8way_1_b), .C(dmux8way_1_c), .D(dmux8way_1_d),
    .E(dmux8way_1_e), .F(dmux8way_1_f), .G(dmux8way_1_g), .H(dmux8way_1_h));
  _8_bit_Register u_8_bit_register_1 (.In(In), .Clock(Clock), .Load(dmux8way_1_a), .Out(n8_bit_register_1_out));
  _8_bit_Register u_8_bit_register_2 (.In(In), .Clock(Clock), .Load(dmux8way_1_b), .Out(n8_bit_register_2_out));
  _8_bit_Register u_8_bit_register_3 (.In(In), .Clock(Clock), .Load(dmux8way_1_c), .Out(n8_bit_register_3_out));
  _8_bit_Register u_8_bit_register_4 (.In(In), .Clock(Clock), .Load(dmux8way_1_d), .Out(n8_bit_register_4_out));
  _8_bit_Register u_8_bit_register_5 (.In(In), .Clock(Clock), .Load(dmux8way_1_e), .Out(n8_bit_register_5_out));
  _8_bit_Register u_8_bit_register_6 (.In(In), .Clock(Clock), .Load(dmux8way_1_f), .Out(n8_bit_register_6_out));
  _8_bit_Register u_8_bit_register_7 (.In(In), .Clock(Clock), .Load(dmux8way_1_g), .Out(n8_bit_register_7_out));
  _8_bit_Register u_8_bit_register_8 (.In(In), .Clock(Clock), .Load(dmux8way_1_h), .Out(n8_bit_register_8_out));
  Mux8Way8 mux8way8_1 (
    .In0(n8_bit_register_1_out), .In1(n8_bit_register_2_out), .In2(n8_bit_register_3_out),
    .In3(n8_bit_register_4_out), .In4(n8_bit_register_5_out), .In5(n8_bit_register_6_out),
    .In6(n8_bit_register_7_out), .In7(n8_bit_register_8_out), .Sel(Sel), .Out(Out));
endmodule

module _8_bit_Register (
  input  [7:0] In,
  input  Clock,
  input  Load,
  output [7:0] Out
);

  Bit bit_1 (.In(In[7]), .Load(Load), .Out(Out[7]), .Clock(Clock));
  Bit bit_2 (.In(In[6]), .Load(Load), .Out(Out[6]), .Clock(Clock));
  Bit bit_3 (.In(In[5]), .Load(Load), .Out(Out[5]), .Clock(Clock));
  Bit bit_4 (.In(In[4]), .Load(Load), .Out(Out[4]), .Clock(Clock));
  Bit bit_5 (.In(In[3]), .Load(Load), .Out(Out[3]), .Clock(Clock));
  Bit bit_6 (.In(In[1]), .Load(Load), .Out(Out[1]), .Clock(Clock));
  Bit bit_7 (.In(In[2]), .Load(Load), .Out(Out[2]), .Clock(Clock));
  Bit bit_8 (.In(In[0]), .Load(Load), .Out(Out[0]), .Clock(Clock));
endmodule

module Bit (
  input  In,
  input  Load,
  input  Clock,
  output Out
);

  wire mux2way_1_out;

  Mux2Way mux2way_1 (.A(Out), .B(In), .Out(mux2way_1_out), .Sel(Load));
  D_FF d_ff_1 (.D(mux2way_1_out), .Clock(Clock), .Q(Out));  // open: Q_prime
endmodule

module Mux8Way8 (
  input  [7:0] In0,
  input  [7:0] In1,
  input  [7:0] In2,
  input  [7:0] In3,
  input  [7:0] In4,
  input  [7:0] In5,
  input  [7:0] In6,
  input  [7:0] In7,
  input  [2:0] Sel,
  output [7:0] Out
);

  wire [7:0] mux4way8_1_out, mux4way8_2_out;

  Mux4Way8 mux4way8_1 (.In0(In0), .In1(In1), .In2(In2), .In3(In3), .in_5(Sel[1:0]), .Out(mux4way8_1_out));
  Mux4Way8 mux4way8_2 (.In0(In4), .In1(In5), .In2(In6), .In3(In7), .in_5(Sel[1:0]), .Out(mux4way8_2_out));
  Mux2Way8 mux2way8_1 (.In0(mux4way8_1_out), .In1(mux4way8_2_out), .in_3(Sel[2]), .out_4(Out));
endmodule

module Mux4Way8 (
  input  [7:0] In0,
  input  [7:0] In1,
  input  [7:0] In2,
  input  [7:0] In3,
  input  [1:0] in_5,
  output [7:0] Out
);

  wire [7:0] mux2way8_1_out_4, mux2way8_2_out_4;

  Mux2Way8 mux2way8_1 (.In0(In0), .In1(In1), .in_3(in_5[0]), .out_4(mux2way8_1_out_4));
  Mux2Way8 mux2way8_2 (.In0(In2), .In1(In3), .in_3(in_5[0]), .out_4(mux2way8_2_out_4));
  Mux2Way8 mux2way8_3 (.In0(mux2way8_1_out_4), .In1(mux2way8_2_out_4), .in_3(in_5[1]), .out_4(Out));
endmodule

module Mux2Way8 (
  input  [7:0] In0,
  input  [7:0] In1,
  input  in_3,
  output [7:0] out_4
);

  Mux2Way mux2way_1 (.A(In0[0]), .B(In1[0]), .Out(out_4[0]), .Sel(in_3));
  Mux2Way mux2way_2 (.A(In0[1]), .B(In1[1]), .Out(out_4[1]), .Sel(in_3));
  Mux2Way mux2way_3 (.A(In0[2]), .B(In1[2]), .Out(out_4[2]), .Sel(in_3));
  Mux2Way mux2way_4 (.A(In0[3]), .B(In1[3]), .Out(out_4[3]), .Sel(in_3));
  Mux2Way mux2way_5 (.A(In0[4]), .B(In1[4]), .Out(out_4[4]), .Sel(in_3));
  Mux2Way mux2way_6 (.A(In0[5]), .B(In1[5]), .Out(out_4[5]), .Sel(in_3));
  Mux2Way mux2way_7 (.A(In0[6]), .B(In1[6]), .Out(out_4[6]), .Sel(in_3));
  Mux2Way mux2way_8 (.A(In0[7]), .B(In1[7]), .Out(out_4[7]), .Sel(in_3));
endmodule

module Mux8Way (
  input  in_1,
  input  in_2,
  input  in_3,
  input  in_4,
  input  in_5,
  input  in_6,
  input  in_7,
  input  in_8,
  input  in_9,
  input  in_10,
  input  in_11,
  output out_12
);

  wire mux2way_1_out, mux2way_2_out, mux2way_3_out, mux2way_4_out, mux2way_5_out, mux2way_6_out;

  Mux2Way mux2way_1 (.A(in_1), .B(in_2), .Out(mux2way_1_out), .Sel(in_9));
  Mux2Way mux2way_2 (.A(in_3), .B(in_4), .Out(mux2way_2_out), .Sel(in_9));
  Mux2Way mux2way_3 (.A(in_5), .B(in_6), .Out(mux2way_3_out), .Sel(in_9));
  Mux2Way mux2way_4 (.A(in_7), .B(in_8), .Out(mux2way_4_out), .Sel(in_9));
  Mux2Way mux2way_5 (.A(mux2way_1_out), .B(mux2way_2_out), .Out(mux2way_5_out), .Sel(in_10));
  Mux2Way mux2way_6 (.A(mux2way_3_out), .B(mux2way_4_out), .Out(mux2way_6_out), .Sel(in_10));
  Mux2Way mux2way_7 (.A(mux2way_5_out), .B(mux2way_6_out), .Out(out_12), .Sel(in_11));
endmodule

module Mux4Way (
  input  in_1,
  input  in_2,
  input  in_3,
  input  in_4,
  input  in_5,
  input  in_6,
  output out_7
);

  wire mux2way_1_out, mux2way_2_out;

  Mux2Way mux2way_1 (.A(in_1), .B(in_2), .Out(mux2way_1_out), .Sel(in_5));
  Mux2Way mux2way_2 (.A(in_3), .B(in_4), .Out(mux2way_2_out), .Sel(in_5));
  Mux2Way mux2way_3 (.A(mux2way_1_out), .B(mux2way_2_out), .Out(out_7), .Sel(in_6));
endmodule

module Mux2Way (
  input  A,
  input  B,
  input  Sel,
  output Out
);

  wire and_with_nand_1_out_3, and_with_nand_2_out_3, not_with_nand_1_out_2;

  NOT_with_NAND not_with_nand_1 (.in_1(Sel), .out_2(not_with_nand_1_out_2));
  AND_with_NAND and_with_nand_1 (.in_1(A), .in_2(not_with_nand_1_out_2), .out_3(and_with_nand_1_out_3));
  AND_with_NAND and_with_nand_2 (.in_1(B), .in_2(Sel), .out_3(and_with_nand_2_out_3));
  OR_with_NAND or_with_nand_1 (.in_1(and_with_nand_1_out_3), .in_2(and_with_nand_2_out_3), .out_3(Out));

  // Notes on the sheet:
  //   Out: pull=down
endmodule

module Dmux8Way (
  input  In,
  input  [2:0] in_2,
  output A,
  output B,
  output C,
  output D,
  output E,
  output F,
  output G,
  output H
);

  wire dmux2way_1_a, dmux2way_1_b;

  Dmux2Way dmux2way_1 (.IN(In), .A(dmux2way_1_a), .B(dmux2way_1_b), .SEL(in_2[2]));
  Dmux4Way dmux4way_1 (.In(dmux2way_1_b), .Sel(in_2[1:0]), .A(E), .B(F), .C(G), .D(H));
  Dmux4Way dmux4way_2 (.In(dmux2way_1_a), .Sel(in_2[1:0]), .A(A), .B(B), .C(C), .D(D));
endmodule

module Dmux4Way (
  input  In,
  input  [1:0] Sel,
  output A,
  output B,
  output C,
  output D
);

  wire dmux2way_1_a, dmux2way_1_b;

  Dmux2Way dmux2way_1 (.IN(In), .A(dmux2way_1_a), .B(dmux2way_1_b), .SEL(Sel[1]));
  Dmux2Way dmux2way_2 (.IN(dmux2way_1_a), .A(A), .B(B), .SEL(Sel[0]));
  Dmux2Way dmux2way_3 (.IN(dmux2way_1_b), .A(C), .B(D), .SEL(Sel[0]));
endmodule

module Dmux2Way (
  input  IN,
  input  SEL,
  output A,
  output B
);

  wire not_with_nand_1_out_2;

  NOT_with_NAND not_with_nand_1 (.in_1(SEL), .out_2(not_with_nand_1_out_2));
  AND_with_NAND and_with_nand_1 (.in_1(IN), .in_2(not_with_nand_1_out_2), .out_3(A));
  AND_with_NAND and_with_nand_2 (.in_1(IN), .in_2(SEL), .out_3(B));
endmodule

module D_FF (
  input  D,
  input  Clock,
  output Q,
  output Q_prime
);

  wire nand_1_out, nand_2_out, not_1_out;

  not not_1 (not_1_out, D);
  nand nand_1 (nand_1_out, D, Clock);
  nand nand_2 (nand_2_out, Clock, not_1_out);
  nand nand_3 (Q, nand_1_out, Q_prime);
  nand nand_4 (Q_prime, nand_2_out, Q);

  // Notes on the sheet:
  //   Q_prime: pull=up
  //   Q: pull=down
endmodule

module XOR_with_NAND (
  input  in_1,
  input  in_2,
  output out_3
);

  wire nand_1_out, nand_2_out, nand_3_out, nand_4_out;

  nand nand_1 (nand_1_out, in_1, in_1);
  nand nand_2 (nand_2_out, in_2, in_2);
  nand nand_3 (nand_3_out, in_1, nand_2_out);
  nand nand_4 (nand_4_out, nand_1_out, in_2);
  nand nand_5 (out_3, nand_3_out, nand_4_out);
endmodule

module AND_with_NAND (
  input  in_1,
  input  in_2,
  output out_3
);

  wire nand_1_out;

  nand nand_1 (nand_1_out, in_1, in_2);
  nand nand_2 (out_3, nand_1_out, nand_1_out);

  // Notes on the sheet:
  //   in_1: pull=down
  //   in_2: pull=down
endmodule

module NOT_with_NAND (
  input  in_1,
  output out_2
);

  nand nand_1 (out_2, in_1, in_1);

  // Notes on the sheet:
  //   in_1: pull=down
endmodule

module OR_with_NAND (
  input  in_1,
  input  in_2,
  output out_3
);

  wire nand_1_out, nand_2_out;

  nand nand_1 (nand_1_out, in_1, in_1);
  nand nand_2 (nand_2_out, in_2, in_2);
  nand nand_3 (out_3, nand_1_out, nand_2_out);

  // Notes on the sheet:
  //   in_1: pull=down
  //   out_3: pull=down
  //   in_2: pull=down
endmodule

module T_FF (
  input  T,
  input  Clock,
  output Q,
  output Q_prime
);

  wire and_1_out, and_2_out;

  and and_1 (and_1_out, Q, T, Clock);
  and and_2 (and_2_out, Clock, T, Q_prime);
  nor nor_1 (Q, and_1_out, Q_prime);
  nor nor_2 (Q_prime, Q, and_2_out);
endmodule

module J_K_FF (
  input  J,
  input  Clock,
  input  K,
  output Q,
  output Q_prime
);

  wire and_1_out, and_2_out;

  and and_1 (and_1_out, Q, J, Clock);
  and and_2 (and_2_out, Clock, K, Q_prime);
  nor nor_1 (Q, and_1_out, Q_prime);
  nor nor_2 (Q_prime, Q, and_2_out);
endmodule

module NAND_FF (
  input  Reset,
  input  Set,
  output Q,
  output Q_prime
);

  nand nand_1 (Q, Reset, Q_prime);
  nand nand_2 (Q_prime, Q, Set);
endmodule

module NOR_FF (
  input  Reset,
  input  Set,
  output Q,
  output Q_prime
);

  nor nor_1 (Q, Reset, Q_prime);
  nor nor_2 (Q_prime, Q, Set);
endmodule

module FA (
  input  a,
  input  b,
  input  Cin,
  output S,
  output Cout
);

  wire and_1_out, and_2_out, xor_1_out;

  xor xor_1 (xor_1_out, a, b);
  and and_1 (and_1_out, xor_1_out, Cin);
  and and_2 (and_2_out, a, b);
  xor xor_2 (S, xor_1_out, Cin);
  or or_1 (Cout, and_1_out, and_2_out);
endmodule

module HA (
  input  a,
  input  b,
  output S,
  output Cout
);

  xor xor_1 (S, a, b);
  and and_1 (Cout, a, b);
endmodule

module Transition (
  input  Clock,
  output Clock_prime
);

  wire not_1_out;

  not not_1 (not_1_out, Clock);
  and and_1 (Clock_prime, not_1_out, Clock);
endmodule

module RAM256 (
  input  [7:0] In,
  input  Clock,
  input  Load,
  input  [7:0] in_4,
  output [7:0] out_5
);

  wire dmux8way_1_a, dmux8way_1_b, dmux8way_1_c, dmux8way_1_d, dmux8way_1_e, dmux8way_1_f, dmux8way_1_g,
       dmux8way_1_h;
  wire [7:0] ram32_1_out, ram32_2_out, ram32_3_out, ram32_4_out, ram32_5_out, ram32_6_out, ram32_7_out,
       ram32_8_out;

  Dmux8Way dmux8way_1 (
    .In(Load), .in_2(in_4[7:5]), .A(dmux8way_1_a), .B(dmux8way_1_b), .C(dmux8way_1_c), .D(dmux8way_1_d),
    .E(dmux8way_1_e), .F(dmux8way_1_f), .G(dmux8way_1_g), .H(dmux8way_1_h));
  RAM32 ram32_1 (.In(In), .Load(dmux8way_1_a), .Clock(Clock), .Sel(in_4[4:0]), .Out(ram32_1_out));
  RAM32 ram32_2 (.In(In), .Load(dmux8way_1_b), .Clock(Clock), .Sel(in_4[4:0]), .Out(ram32_2_out));
  RAM32 ram32_3 (.In(In), .Load(dmux8way_1_c), .Clock(Clock), .Sel(in_4[4:0]), .Out(ram32_3_out));
  RAM32 ram32_4 (.In(In), .Load(dmux8way_1_d), .Clock(Clock), .Sel(in_4[4:0]), .Out(ram32_4_out));
  RAM32 ram32_5 (.In(In), .Load(dmux8way_1_e), .Clock(Clock), .Sel(in_4[4:0]), .Out(ram32_5_out));
  RAM32 ram32_6 (.In(In), .Load(dmux8way_1_f), .Clock(Clock), .Sel(in_4[4:0]), .Out(ram32_6_out));
  RAM32 ram32_7 (.In(In), .Load(dmux8way_1_g), .Clock(Clock), .Sel(in_4[4:0]), .Out(ram32_7_out));
  RAM32 ram32_8 (.In(In), .Load(dmux8way_1_h), .Clock(Clock), .Sel(in_4[4:0]), .Out(ram32_8_out));
  Mux8Way8 mux8way8_1 (
    .In0(ram32_1_out), .In1(ram32_2_out), .In2(ram32_3_out), .In3(ram32_4_out), .In4(ram32_5_out),
    .In5(ram32_6_out), .In6(ram32_7_out), .In7(ram32_8_out), .Sel(in_4[7:5]), .Out(out_5));

  // Notes on the sheet:
  //   out_5: pull=down
  //   in_4: pull=down
endmodule
