// Logisim project LittleDropRedesign.circ as structural Verilog
// D2W
module Dmux2Way (
  input  In,
  input  Sel,
  output A,
  output B
);

  wire not_1_out;

  and and_1 (A, In, not_1_out);
  not not_1 (not_1_out, Sel);
  and and_2 (B, In, Sel);
endmodule

// D4W
module Dmux4Way (
  input  In,
  input  [1:0] Sel,
  output A,
  output B,
  output C,
  output D
);

  wire dmux2way_1_a, dmux2way_1_b;

  Dmux2Way dmux2way_1 (.In(In), .Sel(Sel[1]), .A(dmux2way_1_a), .B(dmux2way_1_b));
  Dmux2Way dmux2way_2 (.In(dmux2way_1_a), .Sel(Sel[0]), .A(A), .B(B));
  Dmux2Way dmux2way_3 (.In(dmux2way_1_b), .Sel(Sel[0]), .A(C), .B(D));
endmodule

module Dmux8Way (
  input  In,
  input  [2:0] Sel,
  output A,
  output B,
  output C,
  output D,
  output E,
  output F,
  output G,
  output H
);

  wire dmux2way_1_a, dmux2way_1_b;

  Dmux2Way dmux2way_1 (.In(In), .Sel(Sel[2]), .A(dmux2way_1_a), .B(dmux2way_1_b));
  Dmux4Way dmux4way_1 (.In(dmux2way_1_a), .Sel(Sel[1:0]), .A(A), .B(B), .C(C), .D(D));
  Dmux4Way dmux4way_2 (.In(dmux2way_1_b), .Sel(Sel[1:0]), .A(E), .B(F), .C(G), .D(H));
endmodule

// M2W
module Mux2Way (
  input  A,
  input  B,
  input  Sel,
  output Out
);

  wire and_1_out, and_2_out, not_1_out;

  and and_1 (and_1_out, A, not_1_out);
  not not_1 (not_1_out, Sel);
  and and_2 (and_2_out, B, Sel);
  or or_1 (Out, and_1_out, and_2_out);
endmodule

// M4W
module Mux4Way (
  input  A,
  input  B,
  input  C,
  input  D,
  input  [1:0] Sel,
  output Out
);

  wire mux2way_1_out, mux2way_3_out;

  Mux2Way mux2way_1 (.A(A), .B(B), .Sel(Sel[1]), .Out(mux2way_1_out));
  Mux2Way mux2way_2 (.A(mux2way_1_out), .B(mux2way_3_out), .Sel(Sel[0]), .Out(Out));
  Mux2Way mux2way_3 (.A(C), .B(D), .Sel(Sel[1]), .Out(mux2way_3_out));
endmodule

module Mux8Way (
  input  A,
  input  B,
  input  C,
  input  D,
  input  E,
  input  F,
  input  G,
  input  H,
  input  [2:0] Sel,
  output Sel_2
);

  wire mux2way_1_out, mux2way_2_out, mux2way_3_out, mux2way_4_out, mux2way_5_out, mux2way_6_out;

  Mux2Way mux2way_1 (.A(A), .B(B), .Sel(Sel[2]), .Out(mux2way_1_out));
  Mux2Way mux2way_2 (.A(mux2way_1_out), .B(mux2way_3_out), .Sel(Sel[1]), .Out(mux2way_2_out));
  Mux2Way mux2way_3 (.A(C), .B(D), .Sel(Sel[2]), .Out(mux2way_3_out));
  Mux2Way mux2way_4 (.A(E), .B(F), .Sel(Sel[2]), .Out(mux2way_4_out));
  Mux2Way mux2way_5 (.A(mux2way_4_out), .B(mux2way_6_out), .Sel(Sel[1]), .Out(mux2way_5_out));
  Mux2Way mux2way_6 (.A(G), .B(H), .Sel(Sel[2]), .Out(mux2way_6_out));
  Mux2Way mux2way_7 (.A(mux2way_2_out), .B(mux2way_5_out), .Sel(Sel[0]), .Out(Sel_2));
endmodule

// DFF
module D_FF (
  input  D,
  input  Clock,
  output Q,
  output Q_prime
);

  D_Flip_Flop d_ff_1 (.clk(Clock), .D(D), .Q(Q), .Qn(Q_prime), .en(1'b1));  // open: preset, reset
endmodule

module Bit (
  input  In,
  input  Load,
  input  Clock,
  output Out
);

  wire mux2way_1_out;

  Mux2Way mux2way_1 (.A(Out), .B(In), .Sel(Load), .Out(mux2way_1_out));
  D_FF d_ff_1 (.D(mux2way_1_out), .Clock(Clock), .Q(Out));  // open: Q_prime
endmodule

// 8bR
module _8_bit_Register (
  input  [7:0] In,
  input  Clock,
  input  Load,
  input  [7:0] Out
);

  Bit bit_1 (.In(In[7]), .Load(Load), .Clock(Clock), .Out(Out[7]));
  Bit bit_2 (.In(In[6]), .Load(Load), .Clock(Clock), .Out(Out[6]));
  Bit bit_3 (.In(In[5]), .Load(Load), .Clock(Clock), .Out(Out[5]));
  Bit bit_4 (.In(In[4]), .Load(Load), .Clock(Clock), .Out(Out[4]));
  Bit bit_5 (.In(In[3]), .Load(Load), .Clock(Clock), .Out(Out[3]));
  Bit bit_6 (.In(In[2]), .Load(Load), .Clock(Clock), .Out(Out[2]));
  Bit bit_7 (.In(In[1]), .Load(Load), .Clock(Clock), .Out(Out[1]));
  Bit bit_8 (.In(In[0]), .Load(Load), .Clock(Clock), .Out(Out[0]));
endmodule
