// Logisim project ROM-PC-test.circ as structural Verilog: 1 circuit, main circuit main
module main (
  input  in_1,
  input  [7:0] in_2,
  input  in_3,
  input  in_4,
  input  in_5,
  output [7:0] out_6
);

  wire clock_1_out;
  wire [7:0] rom_1_data;

  ROM rom_1 (.addr(out_6), .data(rom_1_data), .sel(in_5));
  LED led_1 (.in(rom_1_data[6]));
  LED led_2 (.in(rom_1_data[5]));
  LED led_3 (.in(rom_1_data[7]));
  LED led_4 (.in(rom_1_data[2]));
  LED led_5 (.in(rom_1_data[4]));
  LED led_6 (.in(rom_1_data[3]));
  LED led_7 (.in(rom_1_data[1]));
  LED led_8 (.in(rom_1_data[0]));
  Clock clock_1 (.out(clock_1_out));
  Counter counter_1 (.load(in_1), .D(in_2), .count(in_3), .Q(out_6), .clk(clock_1_out), .clr(in_4));  // open: carry

  // Notes on the sheet:
  //   contents of rom_1 (hex, n*v repeats v):
  //   11 fa 5f 0 15 a9 5b ff fe fd fc fb fa 1 fe 49 11 fa 5f 0 15 a9 5b ff fe fd fc fb fa 1 fe 49 11 fa 5f
  //   0 15 a9 5b ff fe fd fc fb fa 1 fe 49 11 fa 5f 0 15 a9 5b ff fe fd fc fb fa 1 fe 49 11 fa 5f 0 15 a9
  //   5b ff fe fd fc fb fa 1 fe 49 11 fa 5f 0 15 a9 5b ff fe fd fc fb fa 1 fe 49 11 fa 5f 0 15 a9 5b ff fe
  //   fd fc fb fa 1 fe 49 11 fa 5f 0 15 a9 5b ff fe fd fc fb fa 1 fe 49 11 fa 5f 0 15 a9 5b ff fe fd fc fb
  //   fa 1 fe 49 11 fa 5f 0 15 a9 5b ff fe fd fc fb fa 1 fe 49 11 fa 5f 0 15 a9 5b ff fe fd fc fb fa 1 fe
  //   49 11 fa 5f 0 15 a9 5b ff fe fd fc fb fa 1 fe 49 11 fa 5f 0 15 a9 5b ff fe fd fc fb fa 1 fe 49 11 fa
  //   5f 0 15 a9 5b ff fe fd fc fb fa 1 fe 49 11 fa 5f 0 15 a9 5b ff fe fd fc fb fa 1 fe 49 11 fa 5f 0 15
  //   a9 5b ff fe fd fc fb fa 1 fe 49
endmodule
