// Logisim project ledMatrix.circ as structural Verilog: 1 circuit, main circuit main
module main (
  input  [7:0] in_1,
  input  in_2,
  input  in_3,
  input  in_4,
  input  in_5,
  output [7:0] out_6
);

  wire clock_1_out;

  Clock clock_1 (.out(clock_1_out));
  // RAM8 ram8_1: pin names not known; wires that end beside it: clock_1_out, in_1, in_2, in_3, in_4, in_5, out_6
  // Probe on out_6[3:0]
  // Probe on out_6[7:4]
  // DotMatrix #(.inputtype("select"), .matrixcols(4), .matrixrows(4)) dotmatrix_1: pin names not known; wires that end beside it: out_6[3:0], out_6[7:4]
endmodule
